// Logisim project FPGANeuralNetwork.circ as structural Verilog
module HiddenLayer (
  input  RESET,
  input  [31:0] WEIGHTS1,
  input  [31:0] NN_INPUT,
  input  [31:0] WEIGHTS2,
  input  [31:0] WEIGHTS3
);

  wire switch_1_p1;

  // Switch switch_1: pin names not known; wires that end beside it: switch_1_p1
  Neuron neuron_1 (
    .RESET(RESET), .INPUT1(NN_INPUT[7:0]), .INPUT2(NN_INPUT[15:8]), .INPUT3(NN_INPUT[23:16]),
    .INPUT4(NN_INPUT[31:24]), .WEIGHT1(WEIGHTS1[7:0]), .WEIGHT2(WEIGHTS1[15:8]), .WEIGHT3(WEIGHTS1[23:16]),
    .WEIGHT4(WEIGHTS1[31:24]), .ENABLE(switch_1_p1));  // open: out_11
  Neuron neuron_2 (
    .RESET(RESET), .INPUT1(NN_INPUT[7:0]), .INPUT2(NN_INPUT[15:8]), .INPUT3(NN_INPUT[23:16]),
    .INPUT4(NN_INPUT[31:24]), .WEIGHT1(WEIGHTS2[7:0]), .WEIGHT2(WEIGHTS2[15:8]), .WEIGHT3(WEIGHTS2[23:16]),
    .WEIGHT4(WEIGHTS2[31:24]), .ENABLE(switch_1_p1));  // open: out_11
  Neuron neuron_3 (
    .RESET(RESET), .INPUT1(NN_INPUT[7:0]), .INPUT2(NN_INPUT[15:8]), .INPUT3(NN_INPUT[23:16]),
    .INPUT4(NN_INPUT[31:24]), .WEIGHT1(WEIGHTS3[7:0]), .WEIGHT2(WEIGHTS3[15:8]), .WEIGHT3(WEIGHTS3[23:16]),
    .WEIGHT4(WEIGHTS3[31:24]), .ENABLE(switch_1_p1));  // open: out_11
endmodule

module main (
);

  wire button_1_out;
  wire [31:0] register_1_q, register_2_q, register_3_q, undriven;

  Register #(.width(32)) register_1 (.Q(register_1_q));  // open: D, en, clk, clr
  Register #(.width(32)) register_2 (.Q(register_2_q));  // open: D, en, clk, clr
  Register #(.width(32)) register_3 (.Q(register_3_q));  // open: D, en, clk, clr
  Button button_1 (.out(button_1_out));
  HiddenLayer hiddenlayer_1 (
    .RESET(button_1_out), .WEIGHTS1(register_1_q), .NN_INPUT(undriven), .WEIGHTS2(register_2_q),
    .WEIGHTS3(register_3_q));
endmodule

module Neuron (
  input  RESET,
  input  [7:0] INPUT1,
  input  [7:0] INPUT2,
  input  [7:0] INPUT3,
  input  [7:0] INPUT4,
  input  [7:0] WEIGHT1,
  input  [7:0] WEIGHT2,
  input  [7:0] WEIGHT3,
  input  [7:0] WEIGHT4,
  input  ENABLE,
  output [7:0] out_11
);

  wire [1:0] counter_1_q;
  wire [7:0] multiplexer_1_out, multiplexer_2_out, multiplier_1_out, register_1_q;

  Counter #(.max('h3), .width(2)) counter_1 (
    .clr(ENABLE), .up(ENABLE), .Q(counter_1_q));  // open: load, count, clk, D, carry
  Multiplexer #(.select(2), .width(8)) multiplexer_1 (
    .in0(INPUT1), .in1(INPUT2), .in2(INPUT3), .in3(INPUT4), .out(multiplexer_1_out), .sel(counter_1_q));
  Multiplexer #(.select(2), .width(8)) multiplexer_2 (
    .in0(WEIGHT1), .in1(WEIGHT2), .in2(WEIGHT3), .in3(WEIGHT4), .out(multiplexer_2_out), .sel(counter_1_q));
  Register register_1 (.D(multiplier_1_out), .en(ENABLE), .clk(ENABLE), .Q(register_1_q));  // open: clr
  Multiplier multiplier_1 (.a(multiplexer_1_out), .b(multiplexer_2_out), .out(multiplier_1_out));  // open: cin, cout
  Sigmoid_Activation_Function sigmoid_activation_function_1 (.x(register_1_q), .y(out_11));

  assign RESET = ENABLE;
endmodule

// VHDL entity Sigmoid_Activation_Function, as the project stores it:
--------------------------------------------------------------------------------
-- Project : FPGA-NN
-- File    : 
-- Autor   :
-- Date    : 
--
--------------------------------------------------------------------------------
-- Description : This is a sigmoid function that takes an 8-bit input vector and outputs an 8-bit result vector.
--
--------------------------------------------------------------------------------

LIBRARY ieee;
USE ieee.std_logic_1164.all;

ENTITY Sigmoid_Activation_Function IS
  PORT (
  ------------------------------------------------------------------------------
  --Insert input ports below
    x        	: IN  std_logic_vector(7 DOWNTO 0); -- input vector example
  ------------------------------------------------------------------------------
  --Insert output ports below
    y        	: OUT std_logic_vector(7 DOWNTO 0)  -- output vector example
    );
END Sigmoid_Activation_Function;

--------------------------------------------------------------------------------
-- VHDL Description
--------------------------------------------------------------------------------

-- Sigmoid function output formula: y = 1 / (1 + e^-x)

ARCHITECTURE Behavioural OF Sigmoid_Activation_Function IS

-- creates a 16-bit wide intermediate signal to aid calculatons
signal temp : std_logic_vector(15 downto 0);

BEGIN

-- takes the negation of our input, and pads it with zeroes to make it 16 bits wide to be saved to the intermediate signal "temp"
temp <= NOT x + "0000000000000001";

-- takes the square negation of our input to save to output "y".
y <= std_logic_vector(unsigned(temp)*unsigned(temp));

END Behavioral;
